# Fritzing sketch TNC 1.3.2 (saved by Fritzing 0.9.3b)
circuit board: 4cm x 5cm
breadboards: 1

parts:
  Arduino_Uno = Arduino Nano (Rev3.0)
  3_5MM_4Pin = TRRS 3.5mm Jack Breakout
  Q1 = NPN-Transistor [package="TO92 [THT]"]
  C1 = Capacitor [package=cap-pth-large]
  C2 = Capacitor [package=cap-pth-large]
  Vin = Screw terminal - 2 pins [package=THT]
  R5 = Resistor [tolerance=±5% resistance=220 package=THT]
  R1 = Resistor [tolerance=±5% resistance=220 package=THT]
  R4 = Resistor [tolerance=±5% resistance=10k package=THT]
  R3 = Resistor [tolerance=±5% resistance=220 package=THT]
  R2 = Resistor [tolerance=±5% resistance=220 package=THT]
  LED1 = LED - 5mm [color="Red (633nm)" package="5 mm [THT]"]
  IIC = female pin header, 2 pins [form="♀ (female)"]

nets:
  N1: Arduino_Uno.GND, 3_5MM_4Pin.SLEEVE, Q1.C, Vin.pin1, R5.Pin_0, R3.Pin_0, LED1.cathode
  N2: Arduino_Uno.D6, R3.Pin_1, R2.Pin_1
  N3: Arduino_Uno.D10, R1.Pin_0
  N4: Arduino_Uno.5V, Vin.pin2, R4.Pin_0
  N5: Arduino_Uno.A5, IIC.pin1
  N6: Arduino_Uno.A4, IIC.pin2
  N7: Arduino_Uno.A0, C2.1, R5.Pin_1, R4.Pin_1
  N8: 3_5MM_4Pin.RING2, C1.2
  N9: 3_5MM_4Pin.RING1, Q1.E
  N10: 3_5MM_4Pin.TIP, C2.2
  N11: Q1.B, R1.Pin_1, LED1.anode
  N12: C1.1, R2.Pin_0

notes:
  KISS
  TNC
  ©©
  LOGAN
  TARVIT
  2019
  V1.3.2
  IIC
  SCL
  SDA
