# Fritzing sketch Diplexer 1.0.0 (saved by Fritzing 0.9.3b)
circuit board: 4.5cm x 2.2cm

parts:
  J$1 = SMA Antenna Connector [package=sma-edge]
  J$2 = SMA Antenna Connector [package=sma-edge]
  J$3 = SMA Antenna Connector [package=sma-edge]
  L3 = Inductor [inductance=68nH package="400 mil [THT]"]
  L4 = Inductor [inductance=100nH package="400 mil [THT]"]
  L5 = Inductor [inductance=68nH package="400 mil [THT]"]
  C1 = Electrolytic Capacitor [capacitance=18pF package="100 mil [THT, electrolytic]"]
  C2 = Electrolytic Capacitor [capacitance=18pF package="100 mil [THT, electrolytic]"]
  C3 = Electrolytic Capacitor [capacitance=18pF package="100 mil [THT, electrolytic]"]
  C4 = Electrolytic Capacitor [capacitance=18pF package="100 mil [THT, electrolytic]"]
  C5 = Electrolytic Capacitor [capacitance=18pF package="100 mil [THT, electrolytic]"]
  L6 = Inductor [inductance=15nH package="400 mil [THT]"]
  L7 = Inductor [package="400 mil [THT]"]

nets:
  GND: J$1.GND, J$2.GND, J$3.GND, C1.-, C2.-, L6.pin_1, L7.pin_1
  N1: J$1.SIGNAL, L3.pin_1
  N2: J$2.SIGNAL, C3.-
  N3: J$3.SIGNAL, L5.pin_0, C5.+
  N4: L3.pin_0, L4.pin_1, C1.+
  N5: L4.pin_0, L5.pin_1, C2.+
  N6: C3.+, C4.-, L6.pin_0
  N7: C4.+, C5.-, L7.pin_0

notes:
  2M
  70CM
  OUT
  DIPLEXER
  LOGAN
  TARVIT
  MM7OWO
