# Fritzing sketch DHCP V2.3.5 (saved by Fritzing 0.9.3b)
circuit board: 6.87832cm x 5.35432cm
breadboards: 1

parts:
  part = female pin header, 8 pins [form="♀ (female)"]
  part_2 = female pin header, 10 pins [form="♀ (female)"]
  part_3 = female pin header, 6 pins [form="♀ (female)"]  # not connected
  part_4 = shrouded pin header, 10 pins [form="♂ (shrouded male)"]
  part_5 = Screw terminal - 2 pins [package=THT]
  part_6 = female pin header, 4 pins [form="♀ (female)"]
  part_7 = female pin header, 4 pins [form="♀ (female)"]
  part_8 = female pin header, 4 pins [form="♀ (female)"]
  part_9 = female pin header, 4 pins [form="♀ (female)"]
  part_10 = female pin header, 4 pins [form="♀ (female)"]
  part_11 = female pin header, 4 pins [form="♀ (female)"]
  part_12 = female pin header, 4 pins [form="♀ (female)"]
  part_13 = Screw terminal - 2 pins [package=THT]
  part_14 = Screw terminal - 2 pins [package=THT]
  part_15 = Screw terminal - 2 pins [package=THT]
  part_16 = Screw terminal - 2 pins [package=THT]
  part_17 = Screw terminal - 2 pins [package=THT]
  RX = LED - 5mm [color="Red (633nm)" package="5 mm [THT]"]
  TX = LED - 5mm [color="Red (633nm)" package="5 mm [THT]"]
  R1 = Resistor [tolerance=±5% resistance=330 package=THT]
  R2 = Resistor [tolerance=±5% resistance=330 package=THT]
  part_18 = female pin header, 4 pins [form="♀ (female)"]
  part_19 = female pin header, 8 pins [form="♀ (female)"]
  PWR = LED - 5mm [color="Red (633nm)" package="5 mm [THT]"]
  R3 = Resistor [tolerance=±5% resistance=330 package=THT]

nets:
  N1: part.pin1, part_17.pin1
  N2: part.pin3, part_4.pin3, part_6.pin4, part_7.pin4, part_8.pin4, part_9.pin4, part_10.pin4, part_11.pin4, part_12.pin4, part_17.pin2, part_18.pin4, PWR.cathode
  N3: part.pin4, part_6.pin1, part_7.pin1, part_8.pin1, part_9.pin1, part_10.pin1, part_11.pin1, part_12.pin1, R1.Pin_0, R2.Pin_0, part_18.pin1, R3.Pin_0
  N4: part_2.pin9, part_13.pin1
  N5: part_2.pin10, part_13.pin2
  N6: part_4.pin2, RX.cathode, part_19.pin1
  N7: part_4.pin10, TX.cathode, part_19.pin2
  N8: part_5.pin1, part_10.pin2, part_11.pin2
  N9: part_5.pin2, part_10.pin3, part_11.pin3
  N10: part_6.pin2, part_16.pin1, part_18.pin2
  N11: part_6.pin3, part_16.pin2, part_18.pin3
  N12: part_7.pin2, part_8.pin2, part_15.pin1
  N13: part_7.pin3, part_8.pin3, part_15.pin2
  N14: part_9.pin2, part_12.pin2, part_14.pin1
  N15: part_9.pin3, part_12.pin3, part_14.pin2
  N16: RX.anode, R1.Pin_1
  N17: TX.anode, R2.Pin_1
  N18: PWR.anode, R3.Pin_1

notes:
  10 PIN
  HC-SR04
  Vin
  IIC
  U1
  U2
  U3
  U4
  DYNAMIC HOME
  COMPUTATIONAL PROBE
  ©© LOGAN TARVIT 2019
  ( DHCP ) VERSION 2.3.5
  TX
  RX
  IDC
  EXT 0
  EXT 1
  D4
  D6
  D5
  D7
  D8
  PWM
  SS
  MOSI
  MISO
  SCK
  GND
  VREF
  SDA
  SCL
  A3
  A2
  A1
  A0
  5V
  3V
  RES
  N/C
  |
  POWER DISTRIBUTION BOARD
