# Fritzing sketch DHCP V2.4.1 (saved by Fritzing 0.9.3b)
circuit board: 6.87832cm x 5.35432cm

parts:
  part = female pin header, 8 pins [form="♀ (female)"]
  J2 = female pin header, 10 pins [form="♀ (female)"]
  part_2 = female pin header, 6 pins [form="♀ (female)"]  # not connected
  J4 = shrouded pin header, 10 pins [form="♂ (shrouded male)"]
  J5 = Screw terminal - 2 pins [package=THT]
  J6 = female pin header, 4 pins [form="♀ (female)"]
  J7 = female pin header, 4 pins [form="♀ (female)"]
  J8 = female pin header, 4 pins [form="♀ (female)"]
  J9 = female pin header, 4 pins [form="♀ (female)"]
  J10 = female pin header, 4 pins [form="♀ (female)"]
  J11 = female pin header, 4 pins [form="♀ (female)"]
  J12 = female pin header, 4 pins [form="♀ (female)"]
  J13 = Screw terminal - 2 pins [package=THT]
  J14 = Screw terminal - 2 pins [package=THT]
  J15 = Screw terminal - 2 pins [package=THT]
  J16 = Screw terminal - 2 pins [package=THT]
  J17 = Screw terminal - 2 pins [package=THT]
  RX = LED - 5mm [color="Red (633nm)" package="5 mm [THT]"]
  TX = LED - 5mm [color="Red (633nm)" package="5 mm [THT]"]
  R1 = Resistor [tolerance=±5% resistance=330 package=THT]
  R2 = Resistor [tolerance=±5% resistance=330 package=THT]
  J18 = female pin header, 4 pins [form="♀ (female)"]
  J19 = female pin header, 8 pins [form="♀ (female)"]
  PWR = LED - 5mm [color="Red (633nm)" package="5 mm [THT]"]
  R3 = Resistor [tolerance=±5% resistance=330 package=THT]
  part_3 = female pin header, 5 pins [form="♀ (female)"]
  R4 = Resistor [tolerance=±5% resistance=330 package=THT]

nets:
  N1: part.pin1, J17.pin1
  N2: part.pin3, J4.pin3, J6.pin4, J7.pin4, J8.pin4, J9.pin4, J10.pin4, J11.pin4, J12.pin4, J17.pin2, J18.pin4, PWR.cathode, part_3.pin5
  N3: part.pin4, J6.pin1, J7.pin1, J8.pin1, J9.pin1, J10.pin1, J11.pin1, J12.pin1, R1.Pin_0, R2.Pin_0, J18.pin1, R3.Pin_0, part_3.pin2, R4.Pin_0
  N4: J2.pin9, J13.pin1
  N5: J2.pin10, J13.pin2
  N6: J4.pin2, RX.cathode, J19.pin1
  N7: J4.pin10, TX.cathode, J19.pin2
  N8: J5.pin1, J10.pin2, J11.pin2
  N9: J5.pin2, J10.pin3, J11.pin3
  N10: J6.pin2, J16.pin1, J18.pin2
  N11: J6.pin3, J16.pin2, J18.pin3
  N12: J7.pin2, J8.pin2, J15.pin1
  N13: J7.pin3, J8.pin3, J15.pin2
  N14: J9.pin2, J12.pin2, J14.pin1
  N15: J9.pin3, J12.pin3, J14.pin2
  N16: RX.anode, R1.Pin_1
  N17: TX.anode, R2.Pin_1
  N18: PWR.anode, R3.Pin_1
  N19: part_3.pin1, part_3.pin3, R4.Pin_1

notes:
  10 PIN
  HC-SR04
  Vin
  IIC
  U1
  U2
  U3
  U4
  DYNAMIC HOME
  COMPUTATIONAL PROBE
  ©© LOGAN TARVIT 2019
  ( DHCP ) VERSION 2.4.1
  TX
  RX
  IDC
  EXT 0
  EXT 1
  D4
  D6
  D5
  D7
  D8
  PWM
  SS
  MOSI
  MISO
  SCK
  GND
  VREF
  SDA
  SCL
  A3
  A2
  A1
  A0
  5V
  3V
  RES
  N/C
  |
  POWER DISTRIBUTION BOARD
